// Logisim project 16BITCPU.circ as structural Verilog: 13 circuits, main circuit main
module CLK (
  input  CLOCK_IN,
  input  CLOCK_ENABLE,
  input  MANUAL_TICK,
  input  HALT,
  output CLOCK_OUT
);

  wire and_1_out, and_2_out, not_1_out, not_2_out, or_1_out;

  not not_1 (not_1_out, CLOCK_ENABLE);
  and and_1 (and_1_out, CLOCK_IN, CLOCK_ENABLE);
  and and_2 (and_2_out, not_1_out, MANUAL_TICK);
  or or_1 (or_1_out, and_1_out, and_2_out);
  not not_2 (not_2_out, HALT);
  and and_3 (CLOCK_OUT, or_1_out, not_2_out);
endmodule

module main (
  input  in_1,
  input  in_2
);

  wire A_AND_B, A_NAND_B, A_NOR_B, A_OR_B, A_XOR_B, ACC_READ, ACC_WRITE, ADD, ADDRESS_WRITE,
       alu_1_borror_out, alu_1_carry_out, alu_1_equals, alu_1_greater, alu_1_lesser, alu_1_zero_flag,
       button_1_out, CARRY_FLAG, clk_1_clock_out, clock_1_out, CMP, CTN_ENB, CTN_OUT, DATA_WRITE,
       decoder_1_out6, EQUALS_FLAG, GERATER_FLAG, HALT, INSTRUCT_READ, INSTRUCT_WRITE, JUMP, KB_REG_LOAD,
       KB_REG_READ, LESS_FLAG, MAR_READ, MAR_WRITE, not_1_out, NOT_A, or_1_out, or_2_out, RAM_READ,
       RAM_WRITE, READ_B, READ_X, READ_Y, RESET_FLAGS, STACK_DATA_READ, STACK_DOWN, STACK_UP, STACK_WRITE,
       STEP_CTN_RESET, SUB, TTY_WRITE, UPDATE_DISPLAY, UPPER_BITS_READ, WRITE_B, WRITE_X, WRITE_Y, ZERO_FLAG;
  wire [3:0] dipswitch_2_sw3, dipswitch_2_sw7, step_counter_1_data_out;
  wire [6:0] keyboard_1_data;
  wire [7:0] frame_buffer_1_out_9, frame_buffer_1_out_10, frame_buffer_1_out_11, frame_buffer_1_out_12,
       frame_buffer_1_out_13, frame_buffer_1_out_14, frame_buffer_1_out_15, frame_buffer_1_out_16;
  wire [14:0] dipswitch_3_sw3;
  wire [14:7] rom_3_data;
  wire [15:0] accumulator_1_always_out, b_register_1_always_out, instruction_register_1_always_out,
       memory_address_register_1_always_out, multiplexer_1_out, program_counter_1_always_out, ram_1_dout,
       stack_1_data_out;

  Pull_Resistor pull_resistor_1 (.node(dipswitch_2_sw3[3]));
  DipSwitch #(.number(5)) dipswitch_1 (
    .sw1(dipswitch_3_sw3[14]), .sw2(dipswitch_3_sw3[13]), .sw3(dipswitch_3_sw3[12]),
    .sw4(dipswitch_3_sw3[11]), .sw5(dipswitch_3_sw3[10]));
  DipSwitch #(.number(7)) dipswitch_2 (
    .sw1(dipswitch_2_sw3[2]), .sw2(dipswitch_2_sw3[1]), .sw3(dipswitch_2_sw3[0]), .sw4(dipswitch_2_sw7[3]),
    .sw5(dipswitch_2_sw7[2]), .sw6(dipswitch_2_sw7[1]), .sw7(dipswitch_2_sw7[0]));
  not not_1 (not_1_out, clk_1_clock_out);
  Hex_Digit_Display hex_digit_display_1 (.value(dipswitch_2_sw3));  // open: dp
  Hex_Digit_Display hex_digit_display_2 (.value(dipswitch_2_sw7));  // open: dp
  or or_1 (or_1_out, decoder_1_out6, STEP_CTN_RESET);
  DipSwitch #(.number(3)) dipswitch_3 (.sw1(dipswitch_3_sw3[2]), .sw2(dipswitch_3_sw3[1]), .sw3(dipswitch_3_sw3[0]));
  Multiplexer #(.width(16)) multiplexer_1 (
    .in0({1'b0, CARRY_FLAG, GERATER_FLAG, EQUALS_FLAG, ZERO_FLAG, LESS_FLAG, instruction_register_1_always_out[14:8], step_counter_1_data_out[2:0]}),
    .in1({dipswitch_2_sw3[3], dipswitch_3_sw3[14:10], dipswitch_2_sw3[2:0], dipswitch_2_sw7, dipswitch_3_sw3[2:0]}),
    .out(multiplexer_1_out), .sel(in_2));
  LED led_1 (.in(step_counter_1_data_out[3]));
  STEP_COUNTER step_counter_1 (.RESET(or_1_out), .CLOCK(not_1_out), .DATA_OUT(step_counter_1_data_out));
  ROM #(.addrWidth(16), .dataWidth(16)) rom_1 (
    .addr(multiplexer_1_out),
    .data({STACK_DATA_READ, UPPER_BITS_READ, ACC_READ, CMP, SUB, ADD, STACK_UP, KB_REG_READ, READ_B, READ_Y, READ_X, INSTRUCT_READ, MAR_READ, CTN_ENB, RAM_READ, CTN_OUT}));
  ROM #(.addrWidth(16), .dataWidth(16)) rom_2 (
    .addr(multiplexer_1_out),
    .data({UPDATE_DISPLAY, DATA_WRITE, JUMP, STACK_DOWN, STACK_WRITE, RAM_WRITE, KB_REG_LOAD, TTY_WRITE, ADDRESS_WRITE, WRITE_Y, WRITE_X, RESET_FLAGS, WRITE_B, ACC_WRITE, INSTRUCT_WRITE, MAR_WRITE}));
  ROM #(.addrWidth(16), .dataWidth(16)) rom_3 (
    .addr(multiplexer_1_out),
    .data({HALT, rom_3_data, STEP_CTN_RESET, A_NOR_B, A_NAND_B, A_XOR_B, A_OR_B, A_AND_B, NOT_A}));
  LED led_2 (.in(step_counter_1_data_out[2]));
  LED led_3 (.in(step_counter_1_data_out[1]));
  LED led_4 (.in(step_counter_1_data_out[0]));
  Decoder #(.select(4)) decoder_1 (
    .out6(decoder_1_out6), .sel(step_counter_1_data_out));  // open: out0, out1, out2, out3, out4, out5, out7, out8, out9, out10, out11, out12, out13, out14, out15, en
  STACK stack_1 (
    .STACK_RESET(button_1_out), .STACK_DOWN(STACK_DOWN), .STACKT_UP(STACK_UP), .STACK_WRITE(STACK_WRITE),
    .DATA_IN(stack_1_data_out), .SATCK_READ(STACK_DATA_READ), .CLOCK(clk_1_clock_out),
    .DATA_OUT(stack_1_data_out));
  Clock clock_1 (.out(clock_1_out));
  RAM #(.addrWidth(16), .dataWidth(16), .enables("line")) ram_1 (
    .addr(memory_address_register_1_always_out), .we(RAM_WRITE), .clk(clk_1_clock_out),
    .din(stack_1_data_out), .dout(ram_1_dout));
  LED led_5 (.in(instruction_register_1_always_out[15]));
  LED led_6 (.in(instruction_register_1_always_out[14]));
  LED led_7 (.in(instruction_register_1_always_out[13]));
  LED led_8 (.in(instruction_register_1_always_out[12]));
  LED led_9 (.in(instruction_register_1_always_out[11]));
  LED led_10 (.in(instruction_register_1_always_out[10]));
  LED led_11 (.in(instruction_register_1_always_out[9]));
  LED led_12 (.in(instruction_register_1_always_out[8]));
  LED led_13 (.in(instruction_register_1_always_out[7]));
  LED led_14 (.in(instruction_register_1_always_out[6]));
  LED led_15 (.in(instruction_register_1_always_out[5]));
  CLK clk_1 (
    .CLOCK_IN(clock_1_out), .CLOCK_ENABLE(in_1), .HALT(HALT), .CLOCK_OUT(clk_1_clock_out));  // open: MANUAL_TICK
  MEMORY_ADDRESS_REGISTER memory_address_register_1 (
    .DATA_IN(stack_1_data_out), .MAR_WRITE(MAR_WRITE), .MAR_READ(MAR_READ), .CLOCK(clk_1_clock_out),
    .RESET(button_1_out), .ALWAYS_OUT(memory_address_register_1_always_out), .DATA_OUT(stack_1_data_out));
  INSTRUCTION_REGISTER instruction_register_1 (
    .DATA_IN(stack_1_data_out), .WRITE(INSTRUCT_WRITE), .READ_TO_LOWER(INSTRUCT_READ),
    .READ_TO_UPPER(UPPER_BITS_READ), .CLOCK(clk_1_clock_out), .RESET(button_1_out),
    .OUT_UPPER(stack_1_data_out[15:8]), .OUT_LOWER(stack_1_data_out[7:0]),
    .ALWAYS_OUT(instruction_register_1_always_out));
  LED led_16 (.in(instruction_register_1_always_out[4]));
  LED led_17 (.in(instruction_register_1_always_out[3]));
  LED led_18 (.in(instruction_register_1_always_out[2]));
  LED led_19 (.in(instruction_register_1_always_out[1]));
  assign stack_1_data_out = RAM_READ ? ram_1_dout : 16'bz;  // Controlled_Buffer controlled_buffer_1
  LED led_20 (.in(instruction_register_1_always_out[0]));
  LED led_21 (.in(stack_1_data_out[15]));
  LED led_22 (.in(stack_1_data_out[14]));
  LED led_23 (.in(stack_1_data_out[13]));
  Pull_Resistor pull_resistor_2 (.node(stack_1_data_out[15]));
  Pull_Resistor pull_resistor_3 (.node(stack_1_data_out[14]));
  Pull_Resistor pull_resistor_4 (.node(stack_1_data_out[13]));
  LED led_24 (.in(stack_1_data_out[12]));
  LED led_25 (.in(stack_1_data_out[11]));
  LED led_26 (.in(stack_1_data_out[10]));
  LED led_27 (.in(stack_1_data_out[9]));
  Pull_Resistor pull_resistor_5 (.node(stack_1_data_out[12]));
  Pull_Resistor pull_resistor_6 (.node(stack_1_data_out[11]));
  Pull_Resistor pull_resistor_7 (.node(stack_1_data_out[10]));
  Pull_Resistor pull_resistor_8 (.node(stack_1_data_out[9]));
  LED led_28 (.in(stack_1_data_out[8]));
  LED led_29 (.in(stack_1_data_out[7]));
  LED led_30 (.in(stack_1_data_out[6]));
  LED led_31 (.in(stack_1_data_out[5]));
  Pull_Resistor pull_resistor_9 (.node(stack_1_data_out[8]));
  Pull_Resistor pull_resistor_10 (.node(stack_1_data_out[7]));
  Pull_Resistor pull_resistor_11 (.node(stack_1_data_out[6]));
  Pull_Resistor pull_resistor_12 (.node(stack_1_data_out[5]));
  LED led_32 (.in(stack_1_data_out[4]));
  LED led_33 (.in(stack_1_data_out[3]));
  LED led_34 (.in(stack_1_data_out[2]));
  LED led_35 (.in(stack_1_data_out[1]));
  Pull_Resistor pull_resistor_13 (.node(stack_1_data_out[4]));
  Pull_Resistor pull_resistor_14 (.node(stack_1_data_out[3]));
  Pull_Resistor pull_resistor_15 (.node(stack_1_data_out[2]));
  Pull_Resistor pull_resistor_16 (.node(stack_1_data_out[1]));
  LED led_36 (.in(stack_1_data_out[0]));
  Pull_Resistor pull_resistor_17 (.node(stack_1_data_out[0]));
  TTY tty_1 (.data(stack_1_data_out[6:0]), .clk(clk_1_clock_out), .we(TTY_WRITE), .clr(button_1_out));
  LED led_37 (.in(program_counter_1_always_out[15]));
  LED led_38 (.in(program_counter_1_always_out[14]));
  LED led_39 (.in(program_counter_1_always_out[13]));
  LED led_40 (.in(program_counter_1_always_out[12]));
  DotMatrix #(.matrixcols(8), .matrixrows(8)) dotmatrix_1 (
    .col0(frame_buffer_1_out_16), .col1(frame_buffer_1_out_15), .col2(frame_buffer_1_out_14),
    .col3(frame_buffer_1_out_13), .col4(frame_buffer_1_out_12), .col5(frame_buffer_1_out_11),
    .col6(frame_buffer_1_out_10), .col7(frame_buffer_1_out_9));
  LED led_41 (.in(program_counter_1_always_out[11]));
  LED led_42 (.in(program_counter_1_always_out[10]));
  LED led_43 (.in(program_counter_1_always_out[9]));
  LED led_44 (.in(program_counter_1_always_out[8]));
  FRAME_BUFFER frame_buffer_1 (
    .DATA_IN(stack_1_data_out[7:0]), .DATA_WRITE(DATA_WRITE), .ADDRESS_SELECT(stack_1_data_out[2:0]),
    .BUFFER_ADDRESS_WRITE_ENABLE(ADDRESS_WRITE), .CLOCK(clk_1_clock_out), .UPDATE_DISPLAY(UPDATE_DISPLAY),
    .RESET_DISPLAY(button_1_out), .out_9(frame_buffer_1_out_9), .out_10(frame_buffer_1_out_10),
    .out_11(frame_buffer_1_out_11), .out_12(frame_buffer_1_out_12), .out_13(frame_buffer_1_out_13),
    .out_14(frame_buffer_1_out_14), .out_15(frame_buffer_1_out_15), .out_16(frame_buffer_1_out_16));  // open: RESET_BUFFER
  LED led_45 (.in(program_counter_1_always_out[7]));
  LED led_46 (.in(program_counter_1_always_out[6]));
  LED led_47 (.in(program_counter_1_always_out[5]));
  LED led_48 (.in(program_counter_1_always_out[4]));
  PROGRAM_COUNTER program_counter_1 (
    .RESET(button_1_out), .JUMP(JUMP), .COUNTER_ENABLE(CTN_ENB), .CLOCK(clk_1_clock_out),
    .ADRESS_IN(stack_1_data_out), .COUNTER_OUT(CTN_OUT), .ALWAYS_OUT(program_counter_1_always_out),
    .ADDRESS_OUT(stack_1_data_out));
  ACCUMULATOR accumulator_1 (
    .DATA_IN(stack_1_data_out), .A_WRITE(ACC_WRITE), .A_READ(ACC_READ), .CLOCK(clk_1_clock_out),
    .RESET(button_1_out), .ALWAYS_OUT(accumulator_1_always_out), .DATA_OUT(stack_1_data_out));
  ALU alu_1 (
    .A_IN(accumulator_1_always_out), .B_IN(b_register_1_always_out), .ADD(ADD), .SUB(SUB), .NOT_A(NOT_A),
    .A_AND_B(A_AND_B), .A_OR_B(A_OR_B), .A_XOR_B(A_XOR_B), .A_NAND_B(A_NAND_B), .A_NOR_B(A_NOR_B),
    .CARRY_OUT(alu_1_carry_out), .BORROR_OUT(alu_1_borror_out), .GREATER(alu_1_greater),
    .EQUALS(alu_1_equals), .LESSER(alu_1_lesser), .ZERO_FLAG(alu_1_zero_flag), .DATA_OUT(stack_1_data_out));  // open: BORROW_IN, CARRY_IN
  B_REGISTER b_register_1 (
    .DATA_IN(stack_1_data_out), .B_WRITE(WRITE_B), .B_READ(READ_B), .CLOCK(clk_1_clock_out),
    .RESET(button_1_out), .ALWAYS_OUT(b_register_1_always_out), .DATA_OUT(stack_1_data_out));
  X_AND_Y_REGISTERS x_and_y_registers_1 (
    .DATA_IN(stack_1_data_out), .WRITE_X(WRITE_X), .WRITE_Y(WRITE_Y), .READ_X(READ_X), .READ_Y(READ_Y),
    .CLOCK(clk_1_clock_out), .RESET(button_1_out), .DATA_OUT(stack_1_data_out));  // open: X_ALWAYS_OUT, Y_ALWAYS_OUT
  Keyboard keyboard_1 (.clk(KB_REG_LOAD), .data(keyboard_1_data));  // open: re, clr, avail
  LED led_49 (.in(program_counter_1_always_out[3]));
  LED led_50 (.in(program_counter_1_always_out[2]));
  LED led_51 (.in(program_counter_1_always_out[1]));
  LED led_52 (.in(program_counter_1_always_out[0]));
  or or_2 (or_2_out, ADD, SUB);
  assign stack_1_data_out[6:0] = KB_REG_READ ? keyboard_1_data : 7'bz;  // Controlled_Buffer controlled_buffer_2
  Button button_1 (.out(button_1_out));
  FLAGS_REGISTERS flags_registers_1 (
    .CARRY(alu_1_carry_out), .BORROW(alu_1_borror_out), .GREATER(alu_1_greater), .EQUALS(alu_1_equals),
    .LESS(alu_1_lesser), .ZERO(alu_1_zero_flag), .MATH_FLAGS_SET(or_2_out), .COMPARE_FLAGS_SET(CMP),
    .CLOCK(clk_1_clock_out), .RESET(RESET_FLAGS), .CARRY_FLAG(CARRY_FLAG), .GREATER_FLAG(GERATER_FLAG),
    .EQUALS_FLAG(EQUALS_FLAG), .LESS_FLAG(LESS_FLAG), .ZERO_FLAG(ZERO_FLAG));  // open: BORROW_FLAG

  // Notes on the sheet:
  //   contents of rom_1 (hex, n*v repeats v):
  //   1 6 6*0 1 6 10 2 4*0 1 6 10 2 4*0 1 6 10 2 4*0 1 6 10 2 4*0 1 6 10 2 4*0 1 6 10 5*0 1 6 10 1 4*0 1 6
  //   10 5*0 1 6 10 5*0 1 6 10 5*0 1 6 10 2000 4*0 1 6 10 80 4*0 1 6 10 20 4*0 1 6 10 40 4*0 1 6 10 100
  //   4*0 1 6 10 2 400 0 0 0 1 6 10 2 800 0 0 0 1 6 10 2 1000 0 0 0 1 6 10 400 4*0 1 6 10 800 4*0 1 6 6*0
  //   1 6 6*0 1 6 6*0 1 6 6*0 1 6 6*0 1 6 6*0 1 6 6*0 1 6 6*0 1 6 6*0 1 6 6*0 1 6 6*0 1 6 20 40 4*0 1 6 20
  //   2 4*0 1 6 40 5*0 1 6 6*0 1 6 6*0 1 6 6*0 1 6 6*0 1 6 6*0 1 6 6*0 1 6 6*0 1 6 6*0 1 6 6*0 1 6 6*0 1 6
  //   6*0 1 6 6*0 1 6 6*0 1 6 200 1 10 0 0 0 1 6 8000 5*0 1 6 200 1 4000 400 0 0 1 6 6*0 1 6 6*0 1 6 6*0 1
  //   6 6*0 1 6 6*0 1 6 6*0 1 6 6*0 1 6 6*0 1 6 6*0 1 6 6*0 1 6 6*0 1 6 6*0 1 6 6*0 1 6 10 5*0 1 6 10 5*0
  //   1 6 6*0 1 6 10 2 4*0 1 6 10 2 4*0 1 6 6*0 1 6 6*0 1 6 6*0 1 6 6*0 1 6 6*0 1 6 6*0 1 6 6*0 1 6 6*0 1
  //   6 6*0 1 6 6*0 1 6 6*0 1 6 10 5*0 1 6 10 2 4*0 1 6 10 2 4*0 1 6 10 2 4*0 1 6 6*0 1 6 6*0 1 6 6*0 1 6
  //   6*0 1 6 6*0 1 6 6*0 1 6 6*0 1 6 6*0 1 6 6*0 1 6 6*0 1 6 6*0 1 6 6*0 1 6 6*0 1 6 6*0 1 6 6*0 1 6 6*0
  //   1 6 6*0 1 6 6*0 1 6 6*0 1 6 6*0 1 6 6*0 1 6 6*0 1 6 6*0 1 6 6*0 1 6 6*0 1 6 6*0 1 6 6*0 1 6 6*0 1 6
  //   10 5*0 1 6 6*0 1 6 6*0 1 6 6*0 1 6 6*0 1 6 6*0 1 6 40 5*0 1 6 4000 400 2000 0 0 0 1 6 6*0 1 6 6*0 1
  //   6 6*0 1 6 6*0 1 6 6*0 1 6 6*0 1 6 6*0 1 6 6*0 1 6 6*0 1 6 10 2 4*0 1 6 10 2 4*0 1 6 10 2 4*0 1 6 10
  //   2 4*0 1 6 10 2 4*0 1 6 10 5*0 1 6 10 1 4*0 1 6 10 5*0 1 6 10 5*0 1 6 10 5*0 1 6 10 2000 4*0 1 6 10
  //   80 4*0 1 6 10 20 4*0 1 6 10 40 4*0 1 6 10 100 4*0 1 6 10 2 400 0 0 0 1 6 10 2 800 0 0 0 1 6 10 2
  //   1000 0 0 0 1 6 10 400 4*0 1 6 10 800 4*0 1 6 6*0 1 6 6*0 1 6 6*0 1 6 6*0 1 6 6*0 1 6 6*0 1 6 6*0 1 6
  //   6*0 1 6 6*0 1 6 6*0 1 6 6*0 1 6 20 40 4*0 1 6 20 2 4*0 1 6 40 5*0 1 6 6*0 1 6 6*0 1 6 6*0 1 6 6*0 1
  //   6 6*0 1 6 6*0 1 6 6*0 1 6 6*0 1 6 6*0 1 6 6*0 1 6 6*0 1 6 6*0 1 6 6*0 1 6 200 1 10 0 0 0 1 6 8000
  //   5*0 1 6 200 1 4000 400 0 0 1 6 6*0 1 6 6*0 1 6 6*0 1 6 6*0 1 6 6*0 1 6 6*0 1 6 6*0 1 6 6*0 1 6 6*0 1
  //   6 6*0 1 6 6*0 1 6 6*0 1 6 6*0 1 6 10 5*0 1 6 10 5*0 1 6 6*0 1 6 10 2 4*0 1 6 10 2 4*0 1 6 6*0 1 6
  //   6*0 1 6 6*0 1 6 6*0 1 6 6*0 1 6 6*0 1 6 6*0 1 6 6*0 1 6 6*0 1 6 6*0 1 6 6*0 1 6 10 5*0 1 6 10 2 4*0
  //   1 6 10 2 4*0 1 6 10 2 4*0 1 6 6*0 1 6 6*0 1 6 6*0 1 6 6*0 1 6 6*0 1 6 6*0 1 6 6*0 1 6 6*0 1 6 6*0 1
  //   6 6*0 1 6 6*0 1 6 6*0 1 6 6*0 1 6 6*0 1 6 6*0 1 6 6*0 1 6 6*0 1 6 6*0 1 6 6*0 1 6 6*0 1 6 6*0 1 6
  //   6*0 1 6 6*0 1 6 6*0 1 6 6*0 1 6 6*0 1 6 6*0 1 6 6*0 1 6 10 5*0 1 6 10 5*0 1 6 6*0 1 6 6*0 1 6 6*0 1
  //   6 6*0 1 6 40 5*0 1 6 4000 400 2000 0 0 0 1 6 6*0 1 6 6*0 1 6 6*0 1 6 6*0 1 6 6*0 1 6 6*0 1 6 6*0 1 6
  //   6*0 1 6 6*0 1 6 10 2 4*0 1 6 10 2 4*0 1 6 10 2 4*0 1 6 10 2 4*0 1 6 10 2 4*0 1 6 10 5*0 1 6 10 1 4*0
  //   1 6 10 5*0 1 6 10 5*0 1 6 10 5*0 1 6 10 2000 4*0 1 6 10 80 4*0 1 6 10 20 4*0 1 6 10 40 4*0 1 6 10
  //   100 4*0 1 6 10 2 400 0 0 0 1 6 10 2 800 0 0 0 1 6 10 2 1000 0 0 0 1 6 10 400 4*0 1 6 10 800 4*0 1 6
  //   6*0 1 6 6*0 1 6 6*0 1 6 6*0 1 6 6*0 1 6 6*0 1 6 6*0 1 6 6*0 1 6 6*0 1 6 6*0 1 6 6*0 1 6 20 40 4*0 1
  //   6 20 2 4*0 1 6 40 5*0 1 6 6*0 1 6 6*0 1 6 6*0 1 6 6*0 1 6 6*0 1 6 6*0 1 6 6*0 1 6 6*0 1 6 6*0 1 6
  //   6*0 1 6 6*0 1 6 6*0 1 6 6*0 1 6 200 1 10 0 0 0 1 6 8000 5*0 1 6 200 1 4000 400 0 0 1 6 6*0 1 6 6*0 1
  //   6 6*0 1 6 6*0 1 6 6*0 1 6 6*0 1 6 6*0 1 6 6*0 1 6 6*0 1 6 6*0 1 6 6*0 1 6 6*0 1 6 6*0 1 6 10 5*0 1 6
  //   10 5*0 1 6 6*0 1 6 10 2 4*0 1 6 10 2 4*0 1 6 6*0 1 6 6*0 1 6 6*0 1 6 6*0 1 6 6*0 1 6 6*0 1 6 6*0 1 6
  //   6*0 1 6 6*0 1 6 6*0 1 6 6*0 1 6 10 5*0 1 6 10 2 4*0 1 6 10 2 4*0 1 6 10 2 4*0 1 6 6*0 1 6 6*0 1 6
  //   6*0 1 6 6*0 1 6 6*0 1 6 6*0 1 6 6*0 1 6 6*0 1 6 6*0 1 6 6*0 1 6 6*0 1 6 6*0 1 6 6*0 1 6 6*0 1 6 6*0
  //   1 6 6*0 1 6 6*0 1 6 6*0 1 6 6*0 1 6 6*0 1 6 6*0 1 6 6*0 1 6 6*0 1 6 6*0 1 6 6*0 1 6 6*0 1 6 6*0 1 6
  //   6*0 1 6 10 5*0 1 6 6*0 1 6 10 5*0 1 6 6*0 1 6 6*0 1 6 6*0 1 6 40 5*0 1 6 4000 400 2000 0 0 0 1 6 6*0
  //   1 6 6*0 1 6 6*0 1 6 6*0 1 6 6*0 1 6 6*0 1 6 6*0 1 6 6*0 1 6 6*0 1 6 10 2 4*0 1 6 10 2 4*0 1 6 10 2
  //   4*0 1 6 10 2 4*0 1 6 10 2 4*0 1 6 10 5*0 1 6 10 1 4*0 1 6 10 5*0 1 6 10 5*0 1 6 10 5*0 1 6 10 2000
  //   4*0 1 6 10 80 4*0 1 6 10 20 4*0 1 6 10 40 4*0 1 6 10 200 4*0 1 6 10 2 400 0 0 0 1 6 10 2 800 0 0 0 1
  //   6 10 2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
  //   contents of rom_2 (hex, n*v repeats v):
  //   1 2 6*0 1 2 1 4 4*0 1 2 1 8 4*0 1 2 1 20 4*0 1 2 1 40 4*0 1 2 1 100 4*0 1 2 4 5*0 1 2 8 5*0 1 2 20
  //   5*0 1 2 40 5*0 1 2 100 5*0 1 2 1 400 4*0 1 2 1 400 4*0 1 2 1 400 4*0 1 2 1 400 4*0 1 2 1 400 200 0 0
  //   0 1 2 1 8 4 0 0 0 1 2 1 8 4 0 0 0 1 2 1 8 4*0 1 2 8 4 4*0 1 2 8 4 4*0 1 2 6*0 1 2 6*0 1 2 6*0 1 2
  //   6*0 1 2 6*0 1 2 6*0 1 2 6*0 1 2 6*0 1 2 6*0 1 2 6*0 1 2 6*0 1 2 1 400 4*0 1 2 1 40 4*0 1 2 100 5*0 1
  //   2 6*0 1 2 6*0 1 2 6*0 1 2 6*0 1 2 6*0 1 2 6*0 1 2 6*0 1 2 6*0 1 2 6*0 1 2 6*0 1 2 6*0 1 2 6*0 1 2
  //   6*0 1 2 0 800 2000 0 0 0 1 2 2000 800 1000 0 0 0 1 2 0 800 8 2000 0 0 1 2 6*0 1 2 6*0 1 2 6*0 1 2
  //   6*0 1 2 6*0 1 2 6*0 1 2 6*0 1 2 6*0 1 2 6*0 1 2 6*0 1 2 6*0 1 2 6*0 1 2 6*0 1 2 80 5*0 1 2 4000 5*0
  //   1 2 8000 5*0 1 2 1 80 4*0 1 2 1 4000 4*0 1 2 6*0 1 2 6*0 1 2 6*0 1 2 6*0 1 2 6*0 1 2 6*0 1 2 6*0 1 2
  //   6*0 1 2 6*0 1 2 6*0 1 2 6*0 1 2 1 400 4*0 1 2 1 8 4 0 0 0 1 2 1 8 4 0 0 0 1 2 1 8 4 0 0 0 1 2 6*0 1
  //   2 6*0 1 2 6*0 1 2 6*0 1 2 6*0 1 2 6*0 1 2 6*0 1 2 6*0 1 2 6*0 1 2 6*0 1 2 6*0 1 2 6*0 1 2 6*0 1 2
  //   6*0 1 2 6*0 1 2 6*0 1 2 6*0 1 2 6*0 1 2 6*0 1 2 6*0 1 2 6*0 1 2 6*0 1 2 6*0 1 2 6*0 1 2 6*0 1 2 6*0
  //   1 2 6*0 1 2 6*0 1 2 2000 5*0 1 2 6*0 1 2 6*0 1 2 6*0 1 2 6*0 1 2 6*0 1 2 2000 5*0 1 2 8 4 2000 0 0 0
  //   1 2 6*0 1 2 6*0 1 2 6*0 1 2 6*0 1 2 6*0 1 2 6*0 1 2 6*0 1 2 6*0 1 2 6*0 1 2 1 4 4*0 1 2 1 8 4*0 1 2
  //   1 20 4*0 1 2 1 40 4*0 1 2 1 100 4*0 1 2 4 5*0 1 2 8 5*0 1 2 20 5*0 1 2 40 5*0 1 2 100 5*0 1 2 1 400
  //   4*0 1 2 1 400 4*0 1 2 1 400 4*0 1 2 1 400 4*0 1 2 1 400 200 0 0 0 1 2 1 8 4 0 0 0 1 2 1 8 4 0 0 0 1
  //   2 1 8 4*0 1 2 8 4 4*0 1 2 8 4 4*0 1 2 6*0 1 2 6*0 1 2 6*0 1 2 6*0 1 2 6*0 1 2 6*0 1 2 6*0 1 2 6*0 1
  //   2 6*0 1 2 6*0 1 2 6*0 1 2 1 400 4*0 1 2 1 40 4*0 1 2 100 5*0 1 2 6*0 1 2 6*0 1 2 6*0 1 2 6*0 1 2 6*0
  //   1 2 6*0 1 2 6*0 1 2 6*0 1 2 6*0 1 2 6*0 1 2 6*0 1 2 6*0 1 2 6*0 1 2 0 800 2000 0 0 0 1 2 2000 800
  //   1000 0 0 0 1 2 0 800 8 2000 0 0 1 2 6*0 1 2 6*0 1 2 6*0 1 2 6*0 1 2 6*0 1 2 6*0 1 2 6*0 1 2 6*0 1 2
  //   6*0 1 2 6*0 1 2 6*0 1 2 6*0 1 2 6*0 1 2 80 5*0 1 2 4000 5*0 1 2 8000 5*0 1 2 1 80 4*0 1 2 1 4000 4*0
  //   1 2 6*0 1 2 6*0 1 2 6*0 1 2 6*0 1 2 6*0 1 2 6*0 1 2 6*0 1 2 6*0 1 2 6*0 1 2 6*0 1 2 6*0 1 2 1 400
  //   4*0 1 2 1 8 4 0 0 0 1 2 1 8 4 0 0 0 1 2 1 8 4 0 0 0 1 2 6*0 1 2 6*0 1 2 6*0 1 2 6*0 1 2 6*0 1 2 6*0
  //   1 2 6*0 1 2 6*0 1 2 6*0 1 2 6*0 1 2 6*0 1 2 6*0 1 2 6*0 1 2 6*0 1 2 6*0 1 2 6*0 1 2 6*0 1 2 6*0 1 2
  //   6*0 1 2 6*0 1 2 6*0 1 2 6*0 1 2 6*0 1 2 6*0 1 2 6*0 1 2 6*0 1 2 6*0 1 2 6*0 1 2 2000 5*0 1 2 2000 10
  //   4*0 1 2 6*0 1 2 6*0 1 2 6*0 1 2 6*0 1 2 2000 5*0 1 2 8 4 2000 0 0 0 1 2 6*0 1 2 6*0 1 2 6*0 1 2 6*0
  //   1 2 6*0 1 2 6*0 1 2 6*0 1 2 6*0 1 2 6*0 1 2 1 4 4*0 1 2 1 8 4*0 1 2 1 20 4*0 1 2 1 40 4*0 1 2 1 100
  //   4*0 1 2 4 5*0 1 2 8 5*0 1 2 20 5*0 1 2 40 5*0 1 2 100 5*0 1 2 1 400 4*0 1 2 1 400 4*0 1 2 1 400 4*0
  //   1 2 1 400 4*0 1 2 1 400 200 0 0 0 1 2 1 8 4 0 0 0 1 2 1 8 4 0 0 0 1 2 1 8 4*0 1 2 8 4 4*0 1 2 8 4
  //   4*0 1 2 6*0 1 2 6*0 1 2 6*0 1 2 6*0 1 2 6*0 1 2 6*0 1 2 6*0 1 2 6*0 1 2 6*0 1 2 6*0 1 2 6*0 1 2 1
  //   400 4*0 1 2 1 40 4*0 1 2 100 5*0 1 2 6*0 1 2 6*0 1 2 6*0 1 2 6*0 1 2 6*0 1 2 6*0 1 2 6*0 1 2 6*0 1 2
  //   6*0 1 2 6*0 1 2 6*0 1 2 6*0 1 2 6*0 1 2 0 800 2000 0 0 0 1 2 2000 800 1000 0 0 0 1 2 0 800 8 2000 0
  //   0 1 2 6*0 1 2 6*0 1 2 6*0 1 2 6*0 1 2 6*0 1 2 6*0 1 2 6*0 1 2 6*0 1 2 6*0 1 2 6*0 1 2 6*0 1 2 6*0 1
  //   2 6*0 1 2 80 5*0 1 2 4000 5*0 1 2 8000 5*0 1 2 1 80 4*0 1 2 1 4000 4*0 1 2 6*0 1 2 6*0 1 2 6*0 1 2
  //   6*0 1 2 6*0 1 2 6*0 1 2 6*0 1 2 6*0 1 2 6*0 1 2 6*0 1 2 6*0 1 2 1 400 4*0 1 2 1 8 4 0 0 0 1 2 1 8 4
  //   0 0 0 1 2 1 8 4 0 0 0 1 2 6*0 1 2 6*0 1 2 6*0 1 2 6*0 1 2 6*0 1 2 6*0 1 2 6*0 1 2 6*0 1 2 6*0 1 2
  //   6*0 1 2 6*0 1 2 6*0 1 2 6*0 1 2 6*0 1 2 6*0 1 2 6*0 1 2 6*0 1 2 6*0 1 2 6*0 1 2 6*0 1 2 6*0 1 2 6*0
  //   1 2 6*0 1 2 6*0 1 2 6*0 1 2 6*0 1 2 6*0 1 2 6*0 1 2 2000 5*0 1 2 6*0 1 2 2000 10 4*0 1 2 6*0 1 2 6*0
  //   1 2 6*0 1 2 2000 5*0 1 2 8 4 2000 0 0 0 1 2 6*0 1 2 6*0 1 2 6*0 1 2 6*0 1 2 6*0 1 2 6*0 1 2 6*0 1 2
  //   6*0 1 2 6*0 1 2 1 4 4*0 1 2 1 8 4*0 1 2 1 20 4*0 1 2 1 40 4*0 1 2 1 100 4*0 1 2 4 5*0 1 2 8 5*0 1 2
  //   20 5*0 1 2 40 5*0 1 2 100 5*0 1 2 1 400 4*0 1 2 1 400 4*0 1 2 1 400 4*0 1 2 1 400 4*0 1 2 1 400 200
  //   0 0 0 1 2 1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
  //   contents of rom_3 (hex, n*v repeats v):
  //   643*0 1 8*0 2 7*0 4 7*0 8 998*0 1 8*0 2 7*0 4 7*0 8 998*0 1 8*0 2 7*0 4 7*0 8 998*0 1 8*0 2 7*0 4
  //   7*0 8 998*0 1 8*0 2 7*0 4 7*0 8 998*0 1 8*0 2 7*0 4 7*0 8 998*0 1 8*0 2 7*0 4 7*0 8 998*0 1 8*0 2
  //   7*0 4 7*0 8 998*0 1 8*0 2 7*0 4 7*0 8 998*0 1 8*0 2 7*0 4 7*0 8 1007*0 2 7*0 4 7*0 8 1007*0 2 7*0 4
  //   7*0 8 998*0 1 8*0 2 7*0 4 7*0 8 998*0 1 8*0 2 7*0 4 7*0 8 998*0 1 8*0 2 7*0 4 7*0 8 998*0 1 8*0 2
  //   7*0 4 7*0 8 998*0 1 8*0 2 7*0 4 7*0 8 998*0 1 8*0 2 7*0 4 7*0 8 998*0 1 8*0 2 7*0 4 7*0 8 998*0 1
  //   8*0 2 7*0 4 7*0 8 998*0 1 8*0 2 7*0 4 7*0 8 998*0 1 8*0 2 7*0 4 7*0 8 998*0 1 8*0 2 7*0 4 7*0 8
  //   998*0 1 1 7*0 2 7*0 4 0 0 0 4 0 0 0 8 998*0 1 8*0 2 7*0 4 7*0 8 998*0 1 8*0 2 7*0 4 7*0 8 998*0 1
  //   8*0 2 7*0 4 7*0 8 998*0 1 8*0 2 7*0 4 7*0 8 998*0 1 8*0 2 7*0 4 7*0 8 998*0 1 8*0 2 7*0 4 7*0 8
  //   998*0 1 8*0 2 7*0 4 7*0 8 998*0 1 8*0 2 7*0 4 7*0 8
  //   BUS
endmodule

module PROGRAM_COUNTER (
  input  RESET,
  input  JUMP,
  input  COUNTER_ENABLE,
  input  CLOCK,
  input  [15:0] ADRESS_IN,
  input  COUNTER_OUT,
  output [15:0] ALWAYS_OUT,
  output [15:0] ADDRESS_OUT
);

  Counter #(.max('hffff), .width(16)) counter_1 (
    .clr(RESET), .load(JUMP), .up(COUNTER_ENABLE), .count(COUNTER_ENABLE), .clk(CLOCK), .D(ADRESS_IN),
    .Q(ALWAYS_OUT));  // open: carry
  assign ADDRESS_OUT = COUNTER_OUT ? ALWAYS_OUT : 16'bz;  // Controlled_Buffer controlled_buffer_1
endmodule

module ACCUMULATOR (
  input  [15:0] DATA_IN,
  input  A_WRITE,
  input  A_READ,
  input  CLOCK,
  input  RESET,
  output [15:0] ALWAYS_OUT,
  output [15:0] DATA_OUT
);

  Register #(.width(16)) register_1 (.D(DATA_IN), .en(A_WRITE), .clk(CLOCK), .Q(ALWAYS_OUT), .clr(RESET));
  assign DATA_OUT = A_READ ? ALWAYS_OUT : 16'bz;  // Controlled_Buffer controlled_buffer_1
endmodule

module ALU (
  input  BORROW_IN,
  input  CARRY_IN,
  input  [15:0] A_IN,
  input  [15:0] B_IN,
  input  ADD,
  input  SUB,
  input  NOT_A,
  input  A_AND_B,
  input  A_OR_B,
  input  A_XOR_B,
  input  A_NAND_B,
  input  A_NOR_B,
  output CARRY_OUT,
  output BORROR_OUT,
  output GREATER,
  output EQUALS,
  output LESSER,
  output ZERO_FLAG,
  output [15:0] DATA_OUT
);

  wire and_2_out, and_3_out, and_4_out, and_5_out, and_6_out, and_7_out, and_8_out, and_9_out, and_10_out,
       and_11_out, and_12_out, and_13_out, and_14_out, and_15_out, not_2_out, not_3_out, not_4_out,
       not_5_out, not_6_out, not_7_out, not_8_out, not_9_out, not_10_out, not_11_out, not_12_out, not_13_out,
       not_14_out, not_15_out, not_16_out, not_17_out;
  wire [15:0] adder_1_out, and_1_out, nand_1_out, nor_1_out, not_1_out, or_1_out, or_2_out, subtractor_1_out,
       xor_1_out;

  Adder #(.width(16)) adder_1 (.a(A_IN), .b(B_IN), .out(adder_1_out), .cin(CARRY_IN), .cout(CARRY_OUT));
  Subtractor #(.width(16)) subtractor_1 (
    .a(A_IN), .b(B_IN), .out(subtractor_1_out), .bin(BORROW_IN), .bout(BORROR_OUT));
  Comparator #(.width(16)) comparator_1 (.a(A_IN), .b(B_IN), .gt(GREATER), .eq(EQUALS), .lt(LESSER));
  assign not_1_out = ~A_IN;  // NOT_Gate not_1, 16 bits wide
  assign DATA_OUT = ADD ? adder_1_out : 16'bz;  // Controlled_Buffer controlled_buffer_1
  assign DATA_OUT = SUB ? subtractor_1_out : 16'bz;  // Controlled_Buffer controlled_buffer_2
  assign and_1_out = A_IN & B_IN;  // AND_Gate and_1, 16 bits wide
  assign or_1_out = A_IN | B_IN;  // OR_Gate or_1, 16 bits wide
  assign xor_1_out = A_IN ^ B_IN;  // XOR_Gate xor_1, 16 bits wide
  assign nand_1_out = ~(A_IN & B_IN);  // NAND_Gate nand_1, 16 bits wide
  assign nor_1_out = ~(A_IN | B_IN);  // NOR_Gate nor_1, 16 bits wide
  assign DATA_OUT = NOT_A ? not_1_out : 16'bz;  // Controlled_Buffer controlled_buffer_3
  assign DATA_OUT = A_AND_B ? and_1_out : 16'bz;  // Controlled_Buffer controlled_buffer_4
  assign DATA_OUT = A_OR_B ? or_1_out : 16'bz;  // Controlled_Buffer controlled_buffer_5
  assign DATA_OUT = A_XOR_B ? xor_1_out : 16'bz;  // Controlled_Buffer controlled_buffer_6
  assign DATA_OUT = A_NAND_B ? nand_1_out : 16'bz;  // Controlled_Buffer controlled_buffer_7
  assign DATA_OUT = A_NOR_B ? nor_1_out : 16'bz;  // Controlled_Buffer controlled_buffer_8
  assign or_2_out = DATA_OUT;  // OR_Gate or_2, 16 bits wide OR_Gate
  not not_2 (not_2_out, or_2_out[0]);
  not not_3 (not_3_out, or_2_out[1]);
  not not_4 (not_4_out, or_2_out[2]);
  and and_2 (and_2_out, not_2_out, not_3_out);
  and and_3 (and_3_out, and_2_out, not_4_out);
  not not_5 (not_5_out, or_2_out[3]);
  not not_6 (not_6_out, or_2_out[4]);
  not not_7 (not_7_out, or_2_out[5]);
  not not_8 (not_8_out, or_2_out[6]);
  and and_4 (and_4_out, and_3_out, not_5_out);
  and and_5 (and_5_out, and_4_out, not_6_out);
  and and_6 (and_6_out, and_5_out, not_7_out);
  and and_7 (and_7_out, and_6_out, not_8_out);
  not not_9 (not_9_out, or_2_out[7]);
  not not_10 (not_10_out, or_2_out[8]);
  not not_11 (not_11_out, or_2_out[9]);
  not not_12 (not_12_out, or_2_out[10]);
  and and_8 (and_8_out, and_7_out, not_9_out);
  and and_9 (and_9_out, and_8_out, not_10_out);
  and and_10 (and_10_out, and_9_out, not_11_out);
  and and_11 (and_11_out, and_10_out, not_12_out);
  not not_13 (not_13_out, or_2_out[11]);
  not not_14 (not_14_out, or_2_out[12]);
  not not_15 (not_15_out, or_2_out[13]);
  not not_16 (not_16_out, or_2_out[14]);
  and and_12 (and_12_out, and_11_out, not_13_out);
  and and_13 (and_13_out, and_12_out, not_14_out);
  and and_14 (and_14_out, and_13_out, not_15_out);
  and and_15 (and_15_out, and_14_out, not_16_out);
  not not_17 (not_17_out, or_2_out[15]);
  and and_16 (ZERO_FLAG, and_15_out, not_17_out);
  Pull_Resistor pull_resistor_1 (.node(or_2_out[0]));
  Pull_Resistor pull_resistor_2 (.node(or_2_out[1]));
  Pull_Resistor pull_resistor_3 (.node(or_2_out[2]));
  Pull_Resistor pull_resistor_4 (.node(or_2_out[3]));
  Pull_Resistor pull_resistor_5 (.node(or_2_out[4]));
  Pull_Resistor pull_resistor_6 (.node(or_2_out[5]));
  Pull_Resistor pull_resistor_7 (.node(or_2_out[6]));
  Pull_Resistor pull_resistor_8 (.node(or_2_out[7]));
  Pull_Resistor pull_resistor_9 (.node(or_2_out[8]));
  Pull_Resistor pull_resistor_10 (.node(or_2_out[9]));
  Pull_Resistor pull_resistor_11 (.node(or_2_out[10]));
  Pull_Resistor pull_resistor_12 (.node(or_2_out[11]));
  Pull_Resistor pull_resistor_13 (.node(or_2_out[12]));
  Pull_Resistor pull_resistor_14 (.node(or_2_out[13]));
  Pull_Resistor pull_resistor_15 (.node(or_2_out[14]));
  Pull_Resistor pull_resistor_16 (.node(or_2_out[15]));
endmodule

module FLAGS_REGISTERS (
  input  CARRY,
  input  BORROW,
  input  GREATER,
  input  EQUALS,
  input  LESS,
  input  ZERO,
  input  MATH_FLAGS_SET,
  input  COMPARE_FLAGS_SET,
  input  CLOCK,
  input  RESET,
  output CARRY_FLAG,
  output BORROW_FLAG,
  output GREATER_FLAG,
  output EQUALS_FLAG,
  output LESS_FLAG,
  output ZERO_FLAG
);

  Register #(.width(1)) register_1 (.D(CARRY), .en(MATH_FLAGS_SET), .clk(CLOCK), .Q(CARRY_FLAG), .clr(RESET));
  Register #(.width(1)) register_2 (.D(LESS), .en(COMPARE_FLAGS_SET), .clk(CLOCK), .Q(LESS_FLAG), .clr(RESET));
  Register #(.width(1)) register_3 (.D(BORROW), .en(MATH_FLAGS_SET), .clk(CLOCK), .Q(BORROW_FLAG), .clr(RESET));
  Register #(.width(1)) register_4 (.D(GREATER), .en(COMPARE_FLAGS_SET), .clk(CLOCK), .Q(GREATER_FLAG), .clr(RESET));
  Register #(.width(1)) register_5 (.D(EQUALS), .en(COMPARE_FLAGS_SET), .clk(CLOCK), .Q(EQUALS_FLAG), .clr(RESET));
  Register #(.width(1)) register_6 (.D(ZERO), .en(MATH_FLAGS_SET), .clk(CLOCK), .Q(ZERO_FLAG), .clr(RESET));
endmodule

module B_REGISTER (
  input  [15:0] DATA_IN,
  input  B_WRITE,
  input  B_READ,
  input  CLOCK,
  input  RESET,
  output [15:0] ALWAYS_OUT,
  output [15:0] DATA_OUT
);

  Register #(.width(16)) register_1 (.D(DATA_IN), .en(B_WRITE), .clk(CLOCK), .Q(ALWAYS_OUT), .clr(RESET));
  assign DATA_OUT = B_READ ? ALWAYS_OUT : 16'bz;  // Controlled_Buffer controlled_buffer_1
endmodule

module X_AND_Y_REGISTERS (
  input  [15:0] DATA_IN,
  input  WRITE_X,
  input  WRITE_Y,
  input  READ_X,
  input  READ_Y,
  input  CLOCK,
  input  RESET,
  output [15:0] X_ALWAYS_OUT,
  output [15:0] DATA_OUT,
  output [15:0] Y_ALWAYS_OUT
);

  Register #(.width(16)) register_1 (.D(DATA_IN), .en(WRITE_X), .clk(CLOCK), .Q(X_ALWAYS_OUT), .clr(RESET));
  Register #(.width(16)) register_2 (.D(DATA_IN), .en(WRITE_Y), .clk(CLOCK), .Q(Y_ALWAYS_OUT), .clr(RESET));
  assign DATA_OUT = READ_X ? X_ALWAYS_OUT : 16'bz;  // Controlled_Buffer controlled_buffer_1
  assign DATA_OUT = READ_Y ? Y_ALWAYS_OUT : 16'bz;  // Controlled_Buffer controlled_buffer_2
endmodule

module FRAME_BUFFER (
  input  [7:0] DATA_IN,
  input  DATA_WRITE,
  input  [2:0] ADDRESS_SELECT,
  input  BUFFER_ADDRESS_WRITE_ENABLE,
  input  CLOCK,
  input  RESET_BUFFER,
  input  UPDATE_DISPLAY,
  input  RESET_DISPLAY,
  output [7:0] out_9,
  output [7:0] out_10,
  output [7:0] out_11,
  output [7:0] out_12,
  output [7:0] out_13,
  output [7:0] out_14,
  output [7:0] out_15,
  output [7:0] out_16
);

  wire demultiplexer_1_out0, demultiplexer_1_out1, demultiplexer_1_out2, demultiplexer_1_out3,
       demultiplexer_1_out4, demultiplexer_1_out5, demultiplexer_1_out6, demultiplexer_1_out7;
  wire [2:0] register_1_q;
  wire [7:0] register_2_q, register_3_q, register_4_q, register_5_q, register_6_q, register_7_q,
       register_8_q, register_9_q;

  Register #(.width(3)) register_1 (
    .D(ADDRESS_SELECT), .en(BUFFER_ADDRESS_WRITE_ENABLE), .clk(CLOCK), .Q(register_1_q));  // open: clr
  Demultiplexer #(.select(3)) demultiplexer_1 (
    .out0(demultiplexer_1_out0), .out1(demultiplexer_1_out1), .out2(demultiplexer_1_out2),
    .out3(demultiplexer_1_out3), .out4(demultiplexer_1_out4), .out5(demultiplexer_1_out5),
    .out6(demultiplexer_1_out6), .out7(demultiplexer_1_out7), .in(DATA_WRITE), .sel(register_1_q));
  Register register_2 (.D(DATA_IN), .en(demultiplexer_1_out0), .clk(CLOCK), .Q(register_2_q), .clr(RESET_BUFFER));
  Register register_3 (.D(DATA_IN), .en(demultiplexer_1_out1), .clk(CLOCK), .Q(register_3_q));  // open: clr
  Register register_4 (.D(DATA_IN), .en(demultiplexer_1_out2), .clk(CLOCK), .Q(register_4_q), .clr(RESET_BUFFER));
  Register register_5 (.D(DATA_IN), .en(demultiplexer_1_out3), .clk(CLOCK), .Q(register_5_q));  // open: clr
  Register register_6 (.D(DATA_IN), .en(demultiplexer_1_out4), .clk(CLOCK), .Q(register_6_q), .clr(RESET_BUFFER));
  Register register_7 (.D(DATA_IN), .en(demultiplexer_1_out5), .clk(CLOCK), .Q(register_7_q), .clr(RESET_BUFFER));
  Register register_8 (.D(DATA_IN), .en(demultiplexer_1_out6), .clk(CLOCK), .Q(register_8_q), .clr(RESET_BUFFER));
  Register register_9 (.D(DATA_IN), .en(demultiplexer_1_out7), .clk(CLOCK), .Q(register_9_q), .clr(RESET_BUFFER));
  Register register_10 (.D(register_2_q), .en(UPDATE_DISPLAY), .clk(CLOCK), .Q(out_9), .clr(RESET_DISPLAY));
  Register register_11 (.D(register_3_q), .en(UPDATE_DISPLAY), .clk(CLOCK), .Q(out_10), .clr(RESET_DISPLAY));
  Register register_12 (.D(register_4_q), .en(UPDATE_DISPLAY), .clk(CLOCK), .Q(out_11), .clr(RESET_DISPLAY));
  Register register_13 (.D(register_5_q), .en(UPDATE_DISPLAY), .clk(CLOCK), .Q(out_12), .clr(RESET_DISPLAY));
  Register register_14 (.D(register_6_q), .en(UPDATE_DISPLAY), .clk(CLOCK), .Q(out_13), .clr(RESET_DISPLAY));
  Register register_15 (.D(register_7_q), .en(UPDATE_DISPLAY), .clk(CLOCK), .Q(out_14), .clr(RESET_DISPLAY));
  Register register_16 (.D(register_8_q), .en(UPDATE_DISPLAY), .clk(CLOCK), .Q(out_15), .clr(RESET_DISPLAY));
  Register register_17 (.D(register_9_q), .en(UPDATE_DISPLAY), .clk(CLOCK), .Q(out_16), .clr(RESET_DISPLAY));
endmodule

module MEMORY_ADDRESS_REGISTER (
  input  [15:0] DATA_IN,
  input  MAR_WRITE,
  input  MAR_READ,
  input  CLOCK,
  input  RESET,
  output [15:0] ALWAYS_OUT,
  output [15:0] DATA_OUT
);

  Register #(.width(16)) register_1 (.D(DATA_IN), .en(MAR_WRITE), .clk(CLOCK), .Q(ALWAYS_OUT), .clr(RESET));
  assign DATA_OUT = MAR_READ ? ALWAYS_OUT : 16'bz;  // Controlled_Buffer controlled_buffer_1
endmodule

module INSTRUCTION_REGISTER (
  input  [15:0] DATA_IN,
  input  WRITE,
  input  READ_TO_LOWER,
  input  READ_TO_UPPER,
  input  CLOCK,
  input  RESET,
  output [7:0] OUT_UPPER,
  output [7:0] OUT_LOWER,
  output [15:0] ALWAYS_OUT
);

  Register #(.width(16)) register_1 (.D(DATA_IN), .en(WRITE), .clk(CLOCK), .Q(ALWAYS_OUT), .clr(RESET));
  assign OUT_UPPER = READ_TO_UPPER ? ALWAYS_OUT[7:0] : 8'bz;  // Controlled_Buffer controlled_buffer_1
  assign OUT_LOWER = READ_TO_LOWER ? ALWAYS_OUT[7:0] : 8'bz;  // Controlled_Buffer controlled_buffer_2
endmodule

module STEP_COUNTER (
  input  RESET,
  input  CLOCK,
  output [3:0] DATA_OUT
);

  wire undriven;

  Counter #(.max('hf), .width(4)) counter_1 (
    .clr(RESET), .load(undriven), .up(1'b1), .count(1'b1), .clk(CLOCK), .Q(DATA_OUT));  // open: D, carry
endmodule

module STACK (
  input  STACK_RESET,
  input  STACK_DOWN,
  input  STACKT_UP,
  input  STACK_WRITE,
  input  [15:0] DATA_IN,
  input  SATCK_READ,
  input  CLOCK,
  output [15:0] DATA_OUT
);

  wire not_1_out, or_1_out;
  wire [7:0] counter_1_q;
  wire [15:0] ram_1_dout;

  not not_1 (not_1_out, STACK_DOWN);
  or or_1 (or_1_out, STACK_DOWN, STACKT_UP);
  Counter counter_1 (
    .clr(STACK_RESET), .up(not_1_out), .count(or_1_out), .clk(or_1_out), .Q(counter_1_q));  // open: load, D, carry
  RAM #(.dataWidth(16), .enables("line")) ram_1 (
    .addr(counter_1_q), .we(STACK_WRITE), .clk(CLOCK), .din(DATA_IN), .dout(ram_1_dout));
  assign DATA_OUT = SATCK_READ ? ram_1_dout : 16'bz;  // Controlled_Buffer controlled_buffer_1
endmodule
